# Fritzing sketch solaredge_monitor (saved by Fritzing 0.9.9b)

parts:
  WeMos_D1_Mini1 = WeMos D1 Mini
  S1 = Pushbutton [package="[THT]"]
  o1 = Module display OLED I2C 128x64 SSD1306 [package=THT]
  R1 = Resistor [tolerance=±5% power=0.25 resistance=10k package=THT]

nets:
  3V3: WeMos_D1_Mini1.3V3, S1.Pin_3, S1.Pin_4, o1.VCC
  N1: WeMos_D1_Mini1.D1, o1.SCL
  N2: WeMos_D1_Mini1.D2, o1.SDA
  N3: WeMos_D1_Mini1.D5, S1.Pin_1, S1.Pin_2, R1.Pin_1
  N4: WeMos_D1_Mini1.G, o1.GND, R1.Pin_0

custom parts:
  Module display OLED I2C 128x64 SSD1306: Ecran OLED I2C SSD163 de 128x64 avec connexion I2C
